// Logisim project placar-multiesportivo.circ as structural Verilog: 12 circuits, main circuit main
module main (
  input  Enable,
  input  in_2
);

  wire _1_out, _2_out, _3_out, _5_out, _7_out, clock_1_out, codificador_b0, codificador_b1, codificador_b2,
       comparador_1_out_7, conversor_2_b0, conversor_2_b1, conversor_2_b2, conversor_b0, conversor_b1,
       conversor_b2, conversor_b3, decodificador_2_s0, decodificador_2_s1, decodificador_2_s2,
       decodificador_2_s3, decodificador_2_s4, decodificador_2_s5, decodificador_2_s6, decodificador_out_9,
       decodificador_out_11, decodificador_s0, decodificador_s1, decodificador_s2, decodificador_s3,
       decodificador_s5, or_1_out, Undo_out;
  wire [2:0] registrador_3_bits_1_out_8;
  wire [5:0] multiplexer_1_out, registrador_s0_2, somador_6_bits_1_s0, subtractor_1_out;

  Button _1 (.out(_1_out));
  Button _3 (.out(_3_out));
  Button _2 (.out(_2_out));
  Button _7 (.out(_7_out));
  Button _5 (.out(_5_out));
  Button Undo (.out(Undo_out));
  codificador codificador (
    ._1(_1_out), ._2(_2_out), ._3(_3_out), ._5(_5_out), ._7(_7_out), .Enable(Enable), .B2(codificador_b2),
    .B1(codificador_b1), .B0(codificador_b0));
  or or_1 (or_1_out, _1_out, _2_out, _3_out, _5_out, _7_out);
  registrador_3_bits registrador_3_bits_1 (
    .S2(codificador_b2), .S1(codificador_b1), .S0(codificador_b0), .clock(clock_1_out), .enable(or_1_out),
    .out_6(registrador_3_bits_1_out_8[2]), .out_7(registrador_3_bits_1_out_8[1]),
    .out_8(registrador_3_bits_1_out_8[0]));
  Clock clock_1 (.out(clock_1_out));
  Subtractor #(.width(6)) subtractor_1 (
    .a(registrador_s0_2), .b({3'b000, registrador_3_bits_1_out_8}), .out(subtractor_1_out));  // open: bin, bout
  somador_6_bits somador_6_bits_1 (
    .A5(registrador_s0_2[5]), .A4(registrador_s0_2[4]), .A3(registrador_s0_2[3]), .B2(codificador_b2),
    .B1(codificador_b1), .B0(codificador_b0), .A2(registrador_s0_2[2]), .A1(registrador_s0_2[1]),
    .A0(registrador_s0_2[0]), .S5(somador_6_bits_1_s0[5]), .S4(somador_6_bits_1_s0[4]),
    .S3(somador_6_bits_1_s0[3]), .S2(somador_6_bits_1_s0[2]), .S1(somador_6_bits_1_s0[1]),
    .S0(somador_6_bits_1_s0[0]));
  Multiplexer #(.width(6)) multiplexer_1 (
    .in0(somador_6_bits_1_s0), .in1(subtractor_1_out), .out(multiplexer_1_out), .sel(Undo_out), .en(in_2));
  registrador_6_bits registrador (
    .S5(multiplexer_1_out[5]), .S4(multiplexer_1_out[4]), .S3(multiplexer_1_out[3]),
    .S2(multiplexer_1_out[2]), .S1(multiplexer_1_out[1]), .S0(multiplexer_1_out[0]), .clock(clock_1_out),
    .S5_2(registrador_s0_2[5]), .S4_2(registrador_s0_2[4]), .S3_2(registrador_s0_2[3]),
    .S2_2(registrador_s0_2[2]), .S1_2(registrador_s0_2[1]), .S0_2(registrador_s0_2[0]));
  bin____bcd_unidades conversor (
    .S5(registrador_s0_2[5]), .S4(registrador_s0_2[4]), .S3(registrador_s0_2[3]), .S2(registrador_s0_2[2]),
    .S1(registrador_s0_2[1]), .S0(registrador_s0_2[0]), .B3(conversor_b3), .B2(conversor_b2),
    .B1(conversor_b1), .B0(conversor_b0));
  bin__bcd_dezenas conversor_2 (
    .S5(registrador_s0_2[5]), .S4(registrador_s0_2[4]), .S3(registrador_s0_2[3]), .S2(registrador_s0_2[2]),
    .S1(registrador_s0_2[1]), .S0(registrador_s0_2[0]), .B2(conversor_2_b2), .B1(conversor_2_b1),
    .B0(conversor_2_b0));
  comparador comparador_1 (
    .A5(registrador_s0_2[5]), .A4(registrador_s0_2[4]), .A3(registrador_s0_2[3]), .A2(registrador_s0_2[2]),
    .A1(registrador_s0_2[1]), .A0(registrador_s0_2[0]), .out_7(comparador_1_out_7));
  decodificador_4_bits decodificador (
    .A(conversor_b3), .B(conversor_b2), .C(conversor_b1), .D(conversor_b0), .S0(decodificador_s0),
    .S1(decodificador_s1), .S2(decodificador_s2), .S3(decodificador_s3), .out_9(decodificador_out_9),
    .S5(decodificador_s5), .out_11(decodificador_out_11));
  decodificador_3_bits decodificador_2 (
    .A(conversor_2_b2), .B(conversor_2_b1), .C(conversor_2_b0), .S0(decodificador_2_s0),
    .S1(decodificador_2_s1), .S2(decodificador_2_s2), .S3(decodificador_2_s3), .S4(decodificador_2_s4),
    .S5(decodificador_2_s5), .S6(decodificador_2_s6));
  _7_Segment_Display u_7_segment_display_1 (
    .g(decodificador_2_s0), .f(decodificador_2_s1), .a(decodificador_2_s2), .b(decodificador_2_s3),
    .e(decodificador_2_s4), .d(decodificador_2_s5), .c(decodificador_2_s6));  // open: dp
  _7_Segment_Display u_7_segment_display_2 (
    .g(decodificador_s0), .f(decodificador_s1), .a(decodificador_s2), .b(decodificador_s3),
    .e(decodificador_out_9), .d(decodificador_s5), .c(decodificador_out_11));  // open: dp
  LED FIM (.in(comparador_1_out_7));
endmodule

module codificador (
  input  _1,
  input  _2,
  input  _3,
  input  _5,
  input  _7,
  input  Enable,
  output B2,
  output B1,
  output B0
);

  wire or_1_out, or_2_out, or_3_out;

  or or_1 (or_1_out, _5, _7);
  or or_2 (or_2_out, _2, _3, _7);
  or or_3 (or_3_out, _1, _3, _5, _7);
  and and_1 (B2, or_1_out, Enable);
  and and_2 (B1, Enable, or_2_out);
  and and_3 (B0, Enable, or_3_out);
endmodule

module half_adder (
  input  A,
  input  B,
  output S,
  output Cout
);

  xor xor_1 (S, A, B);
  and and_1 (Cout, B, A);
endmodule

module full_adder (
  input  A,
  input  B,
  input  Cin,
  output S,
  output Cout
);

  wire and_1_out, and_2_out, xor_1_out;

  xor xor_1 (xor_1_out, A, B);
  and and_1 (and_1_out, xor_1_out, Cin);
  and and_2 (and_2_out, A, B);
  xor xor_2 (S, xor_1_out, Cin);
  or or_1 (Cout, and_1_out, and_2_out);
endmodule

module somador_6_bits (
  input  A5,
  input  A4,
  input  A3,
  input  B2,
  input  B1,
  input  B0,
  input  A2,
  input  A1,
  input  A0,
  output S5,
  output S4,
  output S3,
  output S2,
  output S1,
  output S0
);

  wire full_adder_2_cout, full_adder_cout, half_adder_2_cout, half_adder_3_cout, half_adder_4_cout;

  half_adder half_adder (.A(A5), .B(half_adder_2_cout), .S(S5));  // open: Cout
  half_adder half_adder_2 (.A(A4), .B(half_adder_3_cout), .S(S4), .Cout(half_adder_2_cout));
  half_adder half_adder_3 (.A(A3), .B(full_adder_cout), .S(S3), .Cout(half_adder_3_cout));
  full_adder full_adder (.A(A2), .B(B2), .Cin(full_adder_2_cout), .S(S2), .Cout(full_adder_cout));
  full_adder full_adder_2 (.A(A1), .B(B1), .Cin(half_adder_4_cout), .S(S1), .Cout(full_adder_2_cout));
  half_adder half_adder_4 (.A(A0), .B(B0), .S(S0), .Cout(half_adder_4_cout));
endmodule

module registrador_6_bits (
  input  S5,
  input  S4,
  input  S3,
  input  S2,
  input  S1,
  input  S0,
  input  clock,
  output S5_2,
  output S4_2,
  output S3_2,
  output S2_2,
  output S1_2,
  output S0_2
);

  D_Flip_Flop d_ff_1 (.clk(clock), .D(S5), .Q(S5_2));  // open: Qn, preset, en, reset
  D_Flip_Flop d_ff_2 (.clk(clock), .D(S4), .Q(S4_2));  // open: Qn, preset, en, reset
  D_Flip_Flop d_ff_3 (.clk(clock), .D(S3), .Q(S3_2));  // open: Qn, preset, en, reset
  D_Flip_Flop d_ff_4 (.clk(clock), .D(S2), .Q(S2_2));  // open: Qn, preset, en, reset
  D_Flip_Flop d_ff_5 (.clk(clock), .D(S1), .Q(S1_2));  // open: Qn, preset, en, reset
  D_Flip_Flop d_ff_6 (.clk(clock), .D(S0), .Q(S0_2));  // open: Qn, preset, en, reset
endmodule

module registrador_3_bits (
  input  S2,
  input  S1,
  input  S0,
  input  clock,
  input  enable,
  output out_6,
  output out_7,
  output out_8
);

  D_Flip_Flop d_ff_1 (.clk(clock), .D(S2), .Q(out_6), .en(enable));  // open: Qn, preset, reset
  D_Flip_Flop d_ff_2 (.clk(clock), .D(S1), .Q(out_7), .en(enable));  // open: Qn, preset, reset
  D_Flip_Flop d_ff_3 (.clk(clock), .D(S0), .Q(out_8), .en(enable));  // open: Qn, preset, reset
endmodule

module bin__bcd_dezenas (
  input  S5,
  input  S4,
  input  S3,
  input  S2,
  input  S1,
  input  S0,
  output B2,
  output B1,
  output B0
);

  wire and_1_out, and_2_out, and_3_out, and_4_out, and_5_out, and_6_out, and_7_out, and_8_out, and_9_out,
       and_10_out, and_11_out, and_12_out, and_13_out, and_14_out, not_1_out, not_2_out, not_3_out,
       not_4_out, not_5_out, not_6_out, not_7_out, not_8_out, not_9_out, not_10_out, not_11_out, not_12_out,
       not_13_out, not_14_out, not_15_out, not_16_out, not_17_out;

  and and_1 (and_1_out, S5, S3);
  and and_2 (and_2_out, S5, S4);
  not not_1 (not_1_out, S5);
  not not_2 (not_2_out, S5);
  not not_3 (not_3_out, S4);
  not not_4 (not_4_out, S3);
  not not_5 (not_5_out, S5);
  not not_6 (not_6_out, S4);
  not not_7 (not_7_out, S5);
  not not_8 (not_8_out, S4);
  not not_9 (not_9_out, S5);
  not not_10 (not_10_out, S5);
  not not_11 (not_11_out, S3);
  not not_12 (not_12_out, S2);
  not not_13 (not_13_out, S4);
  not not_14 (not_14_out, S3);
  not not_15 (not_15_out, S3);
  not not_16 (not_16_out, S3);
  not not_17 (not_17_out, S2);
  or or_1 (B2, and_1_out, and_2_out);
  and and_3 (and_3_out, not_1_out, S4, S2);
  and and_4 (and_4_out, not_2_out, S4, S3);
  and and_5 (and_5_out, S4, S3, S2);
  and and_6 (and_6_out, S5, not_3_out, not_4_out);
  and and_7 (and_7_out, not_5_out, not_6_out, S3, S1);
  and and_8 (and_8_out, not_7_out, not_8_out, S3, S2);
  and and_9 (and_9_out, not_9_out, S3, S2, S1);
  and and_10 (and_10_out, not_10_out, S4, not_11_out, not_12_out);
  and and_11 (and_11_out, S5, not_13_out, not_14_out);
  and and_12 (and_12_out, S5, not_15_out, S1);
  and and_13 (and_13_out, S5, not_16_out, S2);
  and and_14 (and_14_out, S5, S4, S3, not_17_out);
  or or_2 (B1, and_3_out, and_4_out, and_5_out, and_6_out);
  or or_3 (B0, and_7_out, and_8_out, and_9_out, and_10_out, and_11_out, and_12_out, and_13_out, and_14_out);
endmodule

module bin____bcd_unidades (
  input  S5,
  input  S4,
  input  S3,
  input  S2,
  input  S1,
  input  S0,
  output B3,
  output B2,
  output B1,
  output B0
);

  wire and_1_out, and_2_out, and_3_out, and_4_out, and_5_out, and_6_out, and_7_out, and_8_out, and_9_out,
       and_10_out, and_11_out, and_12_out, and_13_out, and_14_out, and_15_out, and_16_out, and_17_out,
       and_18_out, and_19_out, and_20_out, and_21_out, and_22_out, and_23_out, and_24_out, not_1_out,
       not_2_out, not_3_out, not_4_out, not_5_out, not_6_out, not_7_out, not_8_out, not_9_out, not_10_out,
       not_11_out, not_12_out, not_13_out, not_14_out, not_15_out, not_16_out, not_17_out, not_18_out,
       not_19_out, not_20_out, not_21_out, not_22_out, not_23_out, not_24_out, not_25_out, not_26_out,
       not_27_out, not_28_out, not_29_out, not_30_out, not_31_out, not_32_out, not_33_out, not_34_out,
       not_35_out, not_36_out, not_37_out, not_38_out, not_39_out, not_40_out, not_41_out, not_42_out,
       not_43_out, not_44_out, not_45_out, not_46_out, not_47_out, not_48_out, not_49_out, not_50_out,
       not_51_out, not_52_out, not_53_out, not_54_out;

  not not_1 (not_1_out, S5);
  not not_2 (not_2_out, S4);
  not not_3 (not_3_out, S2);
  not not_4 (not_4_out, S1);
  not not_5 (not_5_out, S5);
  not not_6 (not_6_out, S3);
  not not_7 (not_7_out, S2);
  not not_8 (not_8_out, S5);
  not not_9 (not_9_out, S1);
  not not_10 (not_10_out, S4);
  not not_11 (not_11_out, S3);
  not not_12 (not_12_out, S3);
  not not_13 (not_13_out, S2);
  not not_14 (not_14_out, S1);
  not not_15 (not_15_out, S2);
  not not_16 (not_16_out, S4);
  not not_17 (not_17_out, S3);
  not not_18 (not_18_out, S1);
  not not_19 (not_19_out, S5);
  not not_20 (not_20_out, S4);
  not not_21 (not_21_out, S5);
  not not_22 (not_22_out, S2);
  not not_23 (not_23_out, S1);
  not not_24 (not_24_out, S5);
  not not_25 (not_25_out, S2);
  not not_26 (not_26_out, S2);
  not not_27 (not_27_out, S1);
  not not_28 (not_28_out, S4);
  not not_29 (not_29_out, S3);
  not not_30 (not_30_out, S2);
  not not_31 (not_31_out, S4);
  not not_32 (not_32_out, S3);
  not not_33 (not_33_out, S5);
  not not_34 (not_34_out, S4);
  not not_35 (not_35_out, S3);
  not not_36 (not_36_out, S5);
  not not_37 (not_37_out, S3);
  not not_38 (not_38_out, S5);
  not not_39 (not_39_out, S4);
  not not_40 (not_40_out, S1);
  not not_41 (not_41_out, S5);
  not not_42 (not_42_out, S3);
  not not_43 (not_43_out, S2);
  not not_44 (not_44_out, S1);
  not not_45 (not_45_out, S5);
  not not_46 (not_46_out, S2);
  not not_47 (not_47_out, S4);
  not not_48 (not_48_out, S3);
  not not_49 (not_49_out, S1);
  not not_50 (not_50_out, S3);
  not not_51 (not_51_out, S1);
  not not_52 (not_52_out, S4);
  not not_53 (not_53_out, S2);
  not not_54 (not_54_out, S1);
  and and_1 (and_1_out, not_1_out, not_2_out, S3, not_3_out, not_4_out);
  and and_2 (and_2_out, not_5_out, S4, not_6_out, not_7_out, S1);
  and and_3 (and_3_out, not_8_out, S4, S3, S2, not_9_out);
  and and_4 (and_4_out, S5, not_10_out, not_11_out, S2, S1);
  and and_5 (and_5_out, S5, S4, not_12_out, not_13_out, not_14_out);
  and and_6 (and_6_out, S5, S4, S3, not_15_out, S1);
  and and_7 (and_7_out, not_16_out, not_17_out, S2, not_18_out);
  and and_8 (and_8_out, not_19_out, not_20_out, S2, S1);
  and and_9 (and_9_out, not_21_out, S4, not_22_out, not_23_out);
  and and_10 (and_10_out, not_24_out, S4, S3, not_25_out);
  and and_11 (and_11_out, S4, S3, not_26_out, not_27_out);
  and and_12 (and_12_out, S5, not_28_out, not_29_out, not_30_out, S1);
  and and_13 (and_13_out, S5, not_31_out, S3, S2);
  and and_14 (and_14_out, S5, S4, not_32_out, S2, S1);
  and and_15 (and_15_out, not_33_out, not_34_out, not_35_out, S1);
  and and_16 (and_16_out, not_36_out, not_37_out, S2, S1);
  and and_17 (and_17_out, not_38_out, not_39_out, S3, S2, not_40_out);
  and and_18 (and_18_out, not_41_out, S4, not_42_out, not_43_out, not_44_out);
  and and_19 (and_19_out, not_45_out, S4, S3, not_46_out, S1);
  and and_20 (and_20_out, S5, not_47_out, not_48_out, not_49_out);
  and and_21 (and_21_out, S5, not_50_out, S2, not_51_out);
  and and_22 (and_22_out, S5, not_52_out, S3, S1);
  and and_23 (and_23_out, S5, S3, S2, S1);
  and and_24 (and_24_out, S5, S4, S3, not_53_out, not_54_out);
  or or_1 (B3, and_1_out, and_2_out, and_3_out, and_4_out, and_5_out, and_6_out);
  or or_2 (B2, and_7_out, and_8_out, and_9_out, and_10_out, and_11_out, and_12_out, and_13_out, and_14_out);
  or or_3 (B1, and_15_out, and_16_out, and_17_out, and_18_out, and_19_out, and_20_out, and_21_out, and_22_out, and_23_out, and_24_out);

  assign B0 = S0;
endmodule

module decodificador_3_bits (
  input  A,
  input  B,
  input  C,
  output S0,
  output S1,
  output S2,
  output S3,
  output S4,
  output S5,
  output S6
);

  wire and_1_out, and_2_out, and_3_out, and_4_out, and_5_out, and_6_out, and_7_out, and_8_out, and_9_out,
       and_10_out, and_11_out, and_12_out, and_13_out, and_14_out, and_15_out, and_16_out, and_17_out,
       and_18_out, and_19_out, not_1_out, not_2_out, not_3_out;

  not not_1 (not_1_out, B);
  not not_2 (not_2_out, A);
  not not_3 (not_3_out, C);
  and and_1 (and_1_out, not_2_out, B);
  and and_2 (and_2_out, A, not_1_out);
  and and_3 (and_3_out, A, not_3_out);
  and and_4 (and_4_out, A, not_3_out);
  and and_5 (and_5_out, not_1_out, not_3_out);
  and and_6 (and_6_out, A, not_1_out);
  and and_7 (and_7_out, not_2_out, not_3_out);
  and and_8 (and_8_out, B, not_3_out);
  and and_9 (and_9_out, not_2_out, B);
  and and_10 (and_10_out, A, not_1_out, C);
  and and_11 (and_11_out, not_1_out, not_3_out);
  and and_12 (and_12_out, not_2_out, not_3_out);
  and and_13 (and_13_out, B, not_3_out);
  and and_14 (and_14_out, not_2_out, not_3_out);
  and and_15 (and_15_out, B, not_3_out);
  and and_16 (and_16_out, not_2_out, B);
  and and_17 (and_17_out, A, not_1_out, C);
  and and_18 (and_18_out, not_2_out, C);
  and and_19 (and_19_out, A, not_3_out);
  or or_1 (S0, and_1_out, and_2_out, and_3_out);
  or or_2 (S1, and_4_out, and_5_out, and_6_out);
  or or_3 (S2, and_7_out, and_8_out, and_9_out, and_10_out);
  or or_4 (S3, not_2_out, and_11_out);
  or or_5 (S4, and_12_out, and_13_out);
  or or_6 (S5, and_14_out, and_15_out, and_16_out, and_17_out);
  or or_7 (S6, not_1_out, and_18_out, and_19_out);
endmodule

module decodificador_4_bits (
  input  A,
  input  B,
  input  C,
  input  D,
  output S0,
  output S1,
  output S2,
  output S3,
  output out_9,
  output S5,
  output out_11
);

  wire and_1_out, and_2_out, and_3_out, and_4_out, and_5_out, and_6_out, and_7_out, and_8_out, and_9_out,
       and_10_out, and_11_out, and_12_out, and_13_out, and_14_out, and_15_out, and_16_out, and_17_out,
       and_18_out, and_19_out, and_20_out, and_21_out, and_22_out, and_23_out, and_24_out, and_25_out,
       and_26_out, not_1_out, not_2_out, not_3_out, not_4_out;

  not not_1 (not_1_out, A);
  not not_2 (not_2_out, B);
  not not_3 (not_3_out, C);
  not not_4 (not_4_out, D);
  and and_1 (and_1_out, not_1_out, not_2_out, C);
  and and_2 (and_2_out, not_1_out, C, not_4_out);
  and and_3 (and_3_out, not_1_out, B, not_3_out);
  and and_4 (and_4_out, A, not_2_out, not_3_out);
  and and_5 (and_5_out, not_1_out, B, not_4_out);
  and and_6 (and_6_out, not_1_out, not_3_out, B);
  and and_7 (and_7_out, A, not_2_out, not_3_out);
  and and_8 (and_8_out, not_2_out, not_3_out, not_4_out);
  and and_9 (and_9_out, not_1_out, C);
  and and_10 (and_10_out, A, not_2_out, not_3_out);
  and and_11 (and_11_out, not_2_out, not_3_out, not_4_out);
  and and_12 (and_12_out, not_1_out, B, D);
  and and_13 (and_13_out, not_1_out, not_2_out);
  and and_14 (and_14_out, not_2_out, not_3_out);
  and and_15 (and_15_out, not_1_out, not_3_out, not_4_out);
  and and_16 (and_16_out, not_1_out, C, D);
  and and_17 (and_17_out, not_1_out, C, not_4_out);
  and and_18 (and_18_out, not_2_out, not_3_out, not_4_out);
  and and_19 (and_19_out, not_2_out, not_3_out, not_4_out);
  and and_20 (and_20_out, not_1_out, C, not_4_out);
  and and_21 (and_21_out, not_1_out, not_2_out, C);
  and and_22 (and_22_out, not_1_out, B, not_3_out, D);
  and and_23 (and_23_out, not_1_out, B);
  and and_24 (and_24_out, not_1_out, not_3_out);
  and and_25 (and_25_out, not_1_out, D);
  and and_26 (and_26_out, not_2_out, not_3_out);
  or or_1 (S0, and_1_out, and_2_out, and_3_out, and_4_out);
  or or_2 (S1, and_5_out, and_6_out, and_7_out, and_8_out);
  or or_3 (S2, and_9_out, and_10_out, and_11_out, and_12_out);
  or or_4 (S3, and_13_out, and_14_out, and_15_out, and_16_out);
  or or_5 (out_9, and_17_out, and_18_out);
  or or_6 (S5, and_19_out, and_20_out, and_21_out, and_22_out);
  or or_7 (out_11, and_23_out, and_24_out, and_25_out, and_26_out);
endmodule

module comparador (
  input  A5,
  input  A4,
  input  A3,
  input  A2,
  input  A1,
  input  A0,
  output out_7
);

  wire and_1_out, and_2_out, and_3_out, and_4_out;

  and and_1 (and_1_out, A5, A4);
  and and_2 (and_2_out, and_1_out, A3);
  and and_3 (and_3_out, and_1_out, A2);
  and and_4 (and_4_out, and_1_out, A1, A0);
  or or_1 (out_7, and_2_out, and_4_out, and_3_out);
endmodule
